# Fritzing sketch Podmiha (saved by Fritzing 0.9.7b)

parts:
  Part1 = Arduino Nano (Rev3.0)
  S1 = Pushbutton [package="[THT]"]
  Part2 = ws2812b [package="smd 2812b"]
  S2 = Pushbutton [package="[THT]"]
  S3 = Pushbutton [package="[THT]"]
  S4 = Pushbutton [package="[THT]"]
  S5 = Pushbutton [package="[THT]"]

nets:
  GND: Part1.GND, S1.Pin_1, S1.Pin_2, Part2.VSS, S2.Pin_2, S3.Pin_1, S3.Pin_2, S4.Pin_2, S5.Pin_2
  N1: Part1.D2, Part2.DIN
  N2: Part1.D3, S1.Pin_3, S1.Pin_4
  N3: Part1.D4, S2.Pin_3, S2.Pin_4
  N4: Part1.D5, S3.Pin_3, S3.Pin_4
  N5: Part1.D6, S4.Pin_3, S4.Pin_4
  N6: Part1.D7, S5.Pin_3, S5.Pin_4
  5V: Part1.5V, Part2.VDD

notes:
  WS2812 LED
  +5V (for LED)
  GND
  Toggle camera
  Toggle microphone
  Send +
  Send -
  Send screenshot
  UART -> USB
  Arduino nano as example
  Camera & microphone
  status
